// Logisim project exp6-2b.circ as structural Verilog: 1 circuit, main circuit main
module main (
);

  wire and_1_out, bcd_to_7_segment_decoder_1_p1, bcd_to_7_segment_decoder_1_p2,
       bcd_to_7_segment_decoder_1_p3, bcd_to_7_segment_decoder_1_p4, bcd_to_7_segment_decoder_1_p5,
       bcd_to_7_segment_decoder_1_p6, bcd_to_7_segment_decoder_1_p7, bcd_to_7_segment_decoder_1_p8,
       bcd_to_7_segment_decoder_1_p9, bcd_to_7_segment_decoder_1_p10, bcd_to_7_segment_decoder_1_p11,
       bcd_to_7_segment_decoder_1_p12, CLK_out, CLR_out, j_k_ff_1_qn, j_k_ff_3_qn;

  Button CLK (.out(CLK_out));
  // BCD_to_7_segment_decoder bcd_to_7_segment_decoder_1: pin names not known; wires that end beside it: bcd_to_7_segment_decoder_1_p1, bcd_to_7_segment_decoder_1_p2, bcd_to_7_segment_decoder_1_p3, bcd_to_7_segment_decoder_1_p4, bcd_to_7_segment_decoder_1_p5, bcd_to_7_segment_decoder_1_p6, bcd_to_7_segment_decoder_1_p7, bcd_to_7_segment_decoder_1_p8, bcd_to_7_segment_decoder_1_p9, bcd_to_7_segment_decoder_1_p10, bcd_to_7_segment_decoder_1_p11, bcd_to_7_segment_decoder_1_p12
  J_K_Flip_Flop #(.trigger("falling")) j_k_ff_1 (
    .J(1'b1), .clk(CLK_out), .K(1'b1), .Q(bcd_to_7_segment_decoder_1_p1), .Qn(j_k_ff_1_qn), .reset(CLR_out));  // open: preset, en
  Button CLR (.out(CLR_out));
  J_K_Flip_Flop #(.trigger("rising")) j_k_ff_2 (
    .J(j_k_ff_1_qn), .clk(CLK_out), .K(j_k_ff_1_qn), .Q(bcd_to_7_segment_decoder_1_p2), .reset(CLR_out));  // open: Qn, preset, en
  _7_Segment_Display u_7_segment_display_1 (
    .g(bcd_to_7_segment_decoder_1_p11), .f(bcd_to_7_segment_decoder_1_p10),
    .a(bcd_to_7_segment_decoder_1_p5), .b(bcd_to_7_segment_decoder_1_p6), .e(bcd_to_7_segment_decoder_1_p9),
    .d(bcd_to_7_segment_decoder_1_p8), .c(bcd_to_7_segment_decoder_1_p7));  // open: dp
  nor nor_1 (bcd_to_7_segment_decoder_1_p12, bcd_to_7_segment_decoder_1_p1, bcd_to_7_segment_decoder_1_p2);
  J_K_Flip_Flop #(.trigger("rising")) j_k_ff_3 (
    .J(bcd_to_7_segment_decoder_1_p12), .clk(CLK_out), .K(bcd_to_7_segment_decoder_1_p12),
    .Q(bcd_to_7_segment_decoder_1_p3), .Qn(j_k_ff_3_qn), .reset(CLR_out));  // open: preset, en
  and and_1 (and_1_out, bcd_to_7_segment_decoder_1_p12, j_k_ff_3_qn);
  J_K_Flip_Flop #(.trigger("rising")) j_k_ff_4 (
    .J(and_1_out), .clk(CLK_out), .K(and_1_out), .Q(bcd_to_7_segment_decoder_1_p4), .reset(CLR_out));  // open: Qn, preset, en

  // Notes on the sheet:
  //   Nicholas Graca
  //   Section 1
  //   Experiment 6
  //   Due Fri Apr 6th
  //   Activity 2b
endmodule
